# Fritzing sketch Water-Tank-Controller-Labeled (saved by Fritzing 1.0.0)

parts:
  Arduino_Uno = Arduino Uno (Rev3)
  Level_/_A0_/_10k = Rotary Potentiometer (Large) [resistance=10k package=THT]
  Mode_/_D2 = SPST Switch [package=switch-spdt]
  Manual_fill_/_D3 = Round Pushbutton
  Tank_empty_/_D4 = SPST Switch [package=switch-spdt]
  LCD_20x4_I2C_0x27 = 20x4 I2C LCD - illustrative 4-pin module
  Pump_LED_resistor_330_ohm = Resistor [resistance=330 package=THT]
  Pump_/_D8_/_330_ohm = Red LED - 5mm [package="5 mm [THT]"]
  Alarm_LED_resistor_330_ohm = Resistor [resistance=330 package=THT]
  Alarm_/_D9_/_330_ohm = Red LED - 5mm [package="5 mm [THT]"]

nets:
  N1: Arduino_Uno.A0, Level_/_A0_/_10k.wiper
  N2: Arduino_Uno.A4/SDA, LCD_20x4_I2C_0x27.SDA
  N3: Arduino_Uno.A5/SCL, LCD_20x4_I2C_0x27.SCL
  N4: Arduino_Uno.D8, Pump_LED_resistor_330_ohm.Pin_0
  N5: Arduino_Uno.D9_PWM, Alarm_LED_resistor_330_ohm.Pin_0
  GND: Arduino_Uno.GND, Level_/_A0_/_10k.leg1, Mode_/_D2.O, Manual_fill_/_D3.leg1, Tank_empty_/_D4.O, LCD_20x4_I2C_0x27.GND, Pump_/_D8_/_330_ohm.cathode, Alarm_/_D9_/_330_ohm.cathode
  N6: Arduino_Uno.D2, Mode_/_D2.P
  N7: Arduino_Uno.D3_PWM, Manual_fill_/_D3.leg0
  N8: Arduino_Uno.D4, Tank_empty_/_D4.P
  5V: Arduino_Uno.5V, Level_/_A0_/_10k.leg2, LCD_20x4_I2C_0x27.VCC
  N9: Pump_LED_resistor_330_ohm.Pin_1, Pump_/_D8_/_330_ohm.anode
  N10: Alarm_LED_resistor_330_ohm.Pin_1, Alarm_/_D9_/_330_ohm.anode

custom parts:
  20x4 I2C LCD - illustrative 4-pin module: Original teaching representation of an external 20x4 HD44780 LCD with PCF8574 I2C backpack. Verify the labels/order on the actual module. Not a PCB footprint or simulator model.
