# Fritzing sketch Water-Tank-Controller-Wiring (saved by Fritzing 1.0.0)

parts:
  Arduino_Uno_R3 = Arduino Uno (Rev3)
  Level_simulation_-_10k_pot = Rotary Potentiometer (Large) [resistance=10k package=THT]
  Mode_open_AUTO_grounded_MANUAL = SPST Switch [package=switch-spdt]
  Manual_fill_button = Round Pushbutton
  Source-empty_switch = SPST Switch [package=switch-spdt]
  LCD_20x4_I2C_0x27 = 20x4 I2C LCD - illustrative 4-pin module
  Pump_LED_resistor_330_ohm = Resistor [resistance=330 package=THT]
  Pump_command_indicator = Red LED - 5mm [package="5 mm [THT]"]
  Alarm_LED_resistor_330_ohm = Resistor [resistance=330 package=THT]
  Alarm_command_indicator = Red LED - 5mm [package="5 mm [THT]"]

nets:
  N1: Arduino_Uno_R3.A0, Level_simulation_-_10k_pot.wiper
  N2: Arduino_Uno_R3.A4/SDA, LCD_20x4_I2C_0x27.SDA
  N3: Arduino_Uno_R3.A5/SCL, LCD_20x4_I2C_0x27.SCL
  N4: Arduino_Uno_R3.D8, Pump_LED_resistor_330_ohm.Pin_0
  N5: Arduino_Uno_R3.D9_PWM, Alarm_LED_resistor_330_ohm.Pin_0
  GND: Arduino_Uno_R3.GND, Level_simulation_-_10k_pot.leg1, Mode_open_AUTO_grounded_MANUAL.O, Manual_fill_button.leg1, Source-empty_switch.O, LCD_20x4_I2C_0x27.GND, Pump_command_indicator.cathode, Alarm_command_indicator.cathode
  N6: Arduino_Uno_R3.D2, Mode_open_AUTO_grounded_MANUAL.P
  N7: Arduino_Uno_R3.D3_PWM, Manual_fill_button.leg0
  N8: Arduino_Uno_R3.D4, Source-empty_switch.P
  5V: Arduino_Uno_R3.5V, Level_simulation_-_10k_pot.leg2, LCD_20x4_I2C_0x27.VCC
  N9: Pump_LED_resistor_330_ohm.Pin_1, Pump_command_indicator.anode
  N10: Alarm_LED_resistor_330_ohm.Pin_1, Alarm_command_indicator.anode

custom parts:
  20x4 I2C LCD - illustrative 4-pin module: Original teaching representation of an external 20x4 HD44780 LCD with PCF8574 I2C backpack. Verify the labels/order on the actual module. Not a PCB footprint or simulator model.
